# Fritzing sketch OLEDCircuitDiagram (saved by Fritzing 1.0.3b)
breadboards: 1

parts:
  U1 = ESP32-38PinWide [part_number=ESP32-38PinWide]
  Grove1 = Grove OLED 128x96
  S1 = Pushbutton [package="[THT]"]
  S2 = Pushbutton [package="[THT]"]
  S3 = Pushbutton [package="[THT]"]

nets:
  GND: U1.GND, Grove1.GND, S1.Pin_3, S1.Pin_4, S2.Pin_3, S2.Pin_4, S3.Pin_3, S3.Pin_4
  VIN: U1.VIN, Grove1.VCC
  N1: U1.GPIO4, S2.Pin_1, S2.Pin_2
  N2: U1.GPIO18, S3.Pin_1, S3.Pin_2
  N3: U1.GPIO19, S1.Pin_1, S1.Pin_2
  N4: U1.GPIO21, Grove1.SDA
  N5: U1.GPIO23, Grove1.SCL

custom parts:
  ESP32-38PinWide: Generic 38-Pin ESP32 with wide format (only access to one side of pins on a breadboard) based on Stephen Lilley's HiLetgo ESP-WROOM-32 ESP32 ESP-32S Development Board.
